# Fritzing sketch arduino2motors (saved by Fritzing 0.9.3b)

parts:
  Componente1 = Arduino Uno (Rev3)
  Componente2 = Arduino Motor Shield
  Componente3 = Bluetooth HC-05 Macho
  BAT2 = Battery Holders [package=lipo-1100mAh]
  M1 = DC Motor
  M2 = DC Motor

nets:
  N1: Componente1.D9_PWM, Componente2.A2
  N2: Componente1.D10_PWM/SS, Componente2.A1
  N3: Componente1.D11_PWM/MOSI, Componente2.A0
  N4: Componente1.D12/MISO, Componente3.RXD
  N5: Componente1.D13/SCK, Componente3.TXD
  N6: Componente1.D3_PWM, Componente2.A5
  N7: Componente1.D5_PWM, Componente2.A4
  N8: Componente1.D6_PWM, Componente2.A3
  5V: Componente1.5V, Componente3.VCC
  GND: Componente1.GND, Componente3.GND
  N9: Componente2.GND, BAT2.-
  N10: Componente2.VIN, BAT2.+
  N11: Componente2.OUT3, M2.pin_2
  N12: Componente2.OUT4, M2.pin_1
  N13: Componente2.OUT2, M1.pin_2
  N14: Componente2.OUT1, M1.pin_1
